# Fritzing sketch ar_rgb-uln2003-from-500mA-to-1A-per-color-max (saved by Fritzing 0.5.2b)

parts:
  IC1 = ULN2003A [package="DIP16 [THT]"]
  LED1 = RGB LED - (4 legs) [package="5 mm [THT]"]
  Power_plug1 = Power plug
  J1 = screw terminal, 4 pins

nets:
  N1: IC1.In_1, IC1.In_2, J1.pin4
  N2: IC1.In_3, IC1.In_4, J1.pin3
  N3: IC1.In_5, IC1.In_6, J1.pin2
  N4: IC1.0V, Power_plug1.GND, J1.pin1
  N5: IC1.Out_6, IC1.Out_5, LED1.blue_cathode
  N6: IC1.Out_4, IC1.Out_3, LED1.green_cathode
  N7: IC1.Out_2, IC1.Out_1, LED1.red_cathode
  N8: LED1.common_anode, Power_plug1.VCC
