# Fritzing sketch montage (saved by Fritzing 0.6.3b)

parts:
  Arduino1 = Arduino
  Composants1 = SRF05 Ultrasonic Rangefinder

nets:
  N1: Arduino1.GND, Composants1.connector11
  N2: Arduino1.D3, Composants1.connector9
  N3: Arduino1.D2, Composants1.connector10
  N4: Arduino1.+5V, Composants1.connector8
